# Fritzing sketch Lab 3 Sketch (saved by Fritzing 0.9.2b)
breadboards: 1

parts:
  Raspberry_Pi1 = Raspberry Pi 2
  R6 = Resistor [tolerance=±5% resistance=220 package=THT]
  PIR1 = PIR sensor
  LED4 = LED - 5mm [color="Green (555nm)" package="5 mm [THT]"]
  LED5 = LED - 5mm [color="Red (633nm)" package="5 mm [THT]"]
  R7 = Resistor [tolerance=±5% resistance=220 package=THT]

nets:
  GND: Raspberry_Pi1.GND, R6.Pin_0, PIR1.GND, R7.Pin_0
  N1: Raspberry_Pi1.GPIO16, PIR1.SIG
  N2: Raspberry_Pi1.GPIO24, LED5.anode
  N3: Raspberry_Pi1.GPIO23, LED4.anode
  5V: Raspberry_Pi1.5V, PIR1.VDD
  N4: R6.Pin_1, LED4.cathode
  N5: LED5.cathode, R7.Pin_1
